// Logisim project control-logic.circ as structural Verilog: 1 circuit, main circuit control_logic
module control_logic (
  input  [31:0] Instruction,
  input  BrEq,
  input  BrLt,
  output PCSel,
  output RegWEn,
  output [2:0] ImmSel,
  output BrUn,
  output ASel,
  output BSel,
  output [3:0] ALUSel,
  output MemWEn,
  output [1:0] WBSel
);

  wire addi, addR, and_1_out, and_3_out, and_5_out, and_7_out, and_18_out, and_19_out, and_20_out,
       and_21_out, and_24_out, and_33_out, and_34_out, and_35_out, and_36_out, and_37_out, and_39_out,
       and_40_out, and_41_out, and_42_out, and_43_out, andi, andR, auipc, beq, bge, bgeu, blt, bltu, bne,
       comparator_1_eq, comparator_2_eq, comparator_3_eq, comparator_4_eq, comparator_5_eq, comparator_6_eq,
       comparator_7_eq, comparator_8_eq, comparator_9_eq, comparator_10_eq, comparator_11_eq,
       comparator_12_eq, comparator_13_eq, comparator_14_eq, comparator_15_eq, comparator_16_eq,
       comparator_17_eq, comparator_18_eq, comparator_19_eq, comparator_20_eq, comparator_21_eq,
       comparator_22_eq, comparator_23_eq, comparator_24_eq, comparator_25_eq, comparator_26_eq,
       comparator_27_eq, comparator_28_eq, comparator_30_eq, comparator_31_eq, comparator_32_eq,
       comparator_33_eq, comparator_34_eq, comparator_35_eq, comparator_36_eq, comparator_37_eq,
       comparator_38_eq, comparator_39_eq, comparator_40_eq, comparator_41_eq, comparator_42_eq,
       comparator_43_eq, comparator_44_eq, comparator_45_eq, comparator_47_eq, comparator_48_eq,
       comparator_49_eq, comparator_50_eq, comparator_51_eq, comparator_52_eq, comparator_53_eq,
       comparator_54_eq, comparator_55_eq, comparator_56_eq, comparator_57_eq, comparator_59_eq,
       comparator_60_eq, comparator_61_eq, comparator_62_eq, comparator_63_eq, comparator_64_eq,
       comparator_65_eq, comparator_66_eq, comparator_67_eq, comparator_68_eq, comparator_69_eq,
       comparator_70_eq, comparator_71_eq, comparator_72_eq, comparator_73_eq, comparator_74_eq,
       comparator_75_eq, comparator_76_eq, comparator_77_eq, comparator_78_eq, comparator_79_eq,
       comparator_80_eq, comparator_81_eq, comparator_82_eq, comparator_83_eq, comparator_84_eq,
       comparator_85_eq, jal, jalr, lbI, lhI, lui, lwI, mulhR, mulhuR, mulR, not_1_out, not_2_out, not_3_out,
       or_1_out, or_2_out, or_3_out, or_4_out, or_5_out, or_6_out, or_7_out, or_8_out, ori, orR, sbS, shS,
       slli, sllR, slti, sltR, srai, sraR, srli, srlR, subR, swS, xori, xorR;
  wire [5:0] InputROM;
  wire [15:14] rom_1_data;

  Comparator #(.width(7)) comparator_1 (.a(7'b0110011), .b(Instruction[6:0]), .eq(comparator_1_eq));  // open: gt, lt
  Comparator #(.width(7)) comparator_2 (.a(Instruction[31:25]), .b({7{1'b0}}), .eq(comparator_2_eq));  // open: gt, lt
  Comparator #(.width(7)) comparator_3 (.a(7'b0110011), .b(Instruction[6:0]), .eq(comparator_3_eq));  // open: gt, lt
  Comparator #(.width(7)) comparator_4 (.a(Instruction[31:25]), .b(7'b0000001), .eq(comparator_4_eq));  // open: gt, lt
  Comparator #(.width(7)) comparator_5 (.a(7'b0110011), .b(Instruction[6:0]), .eq(comparator_5_eq));  // open: gt, lt
  Comparator #(.width(7)) comparator_6 (.a(Instruction[31:25]), .b(7'b0100000), .eq(comparator_6_eq));  // open: gt, lt
  Comparator #(.width(7)) comparator_7 (.a(7'b0110011), .b(Instruction[6:0]), .eq(comparator_7_eq));  // open: gt, lt
  Comparator #(.width(7)) comparator_8 (.a(Instruction[31:25]), .b({7{1'b0}}), .eq(comparator_8_eq));  // open: gt, lt
  Comparator #(.width(7)) comparator_9 (.a(7'b0000011), .b(Instruction[6:0]), .eq(comparator_9_eq));  // open: gt, lt
  Comparator #(.width(7)) comparator_10 (.a(7'b0010011), .b(Instruction[6:0]), .eq(comparator_10_eq));  // open: gt, lt
  Comparator #(.width(7)) comparator_11 (.a(7'b0010011), .b(Instruction[6:0]), .eq(comparator_11_eq));  // open: gt, lt
  Comparator #(.width(7)) comparator_12 (.a(7'b0010011), .b(Instruction[6:0]), .eq(comparator_12_eq));  // open: gt, lt
  Comparator #(.width(7)) comparator_13 (.a(7'b0010011), .b(Instruction[6:0]), .eq(comparator_13_eq));  // open: gt, lt
  Comparator #(.width(3)) comparator_14 (.a(Instruction[14:12]), .b(3'b000), .eq(comparator_14_eq));  // open: gt, lt
  Comparator #(.width(3)) comparator_15 (.a(Instruction[14:12]), .b(3'b000), .eq(comparator_15_eq));  // open: gt, lt
  Comparator #(.width(3)) comparator_16 (.a(Instruction[14:12]), .b(3'b000), .eq(comparator_16_eq));  // open: gt, lt
  Comparator #(.width(3)) comparator_17 (.a(Instruction[14:12]), .b(3'b001), .eq(comparator_17_eq));  // open: gt, lt
  Comparator #(.width(3)) comparator_18 (.a(Instruction[14:12]), .b(3'b000), .eq(comparator_18_eq));  // open: gt, lt
  Comparator #(.width(3)) comparator_19 (.a(Instruction[14:12]), .b(3'b000), .eq(comparator_19_eq));  // open: gt, lt
  Comparator #(.width(3)) comparator_20 (.a(Instruction[14:12]), .b(3'b100), .eq(comparator_20_eq));  // open: gt, lt
  Comparator #(.width(3)) comparator_21 (.a(Instruction[14:12]), .b(3'b110), .eq(comparator_21_eq));  // open: gt, lt
  Comparator #(.width(3)) comparator_22 (.a(Instruction[14:12]), .b(3'b111), .eq(comparator_22_eq));  // open: gt, lt
  ROM #(.addrWidth(6), .dataWidth(16)) rom_1 (
    .addr(InputROM), .data({rom_1_data, WBSel, MemWEn, ALUSel, BSel, ASel, BrUn, ImmSel, RegWEn}));
  and and_1 (and_1_out, comparator_1_eq, comparator_14_eq);
  and and_2 (addR, and_1_out, comparator_2_eq);
  and and_3 (and_3_out, comparator_3_eq, comparator_15_eq);
  and and_4 (mulR, and_3_out, comparator_4_eq);
  and and_5 (and_5_out, comparator_5_eq, comparator_16_eq);
  and and_6 (subR, and_5_out, comparator_6_eq);
  and and_7 (and_7_out, comparator_7_eq, comparator_17_eq);
  and and_8 (sllR, and_7_out, comparator_8_eq);
  and and_9 (lbI, comparator_9_eq, comparator_18_eq);
  and and_10 (addi, comparator_10_eq, comparator_19_eq);
  and and_11 (xori, comparator_11_eq, comparator_20_eq);
  and and_12 (ori, comparator_12_eq, comparator_21_eq);
  and and_13 (andi, comparator_13_eq, comparator_22_eq);
  Comparator #(.width(7)) comparator_23 (.a(7'b0100011), .b(Instruction[6:0]), .eq(comparator_23_eq));  // open: gt, lt
  Comparator #(.width(7)) comparator_24 (.a(7'b1100011), .b(Instruction[6:0]), .eq(comparator_24_eq));  // open: gt, lt
  Comparator #(.width(7)) comparator_25 (.a(7'b1100011), .b(Instruction[6:0]), .eq(comparator_25_eq));  // open: gt, lt
  and and_14 (sbS, comparator_23_eq, comparator_26_eq);
  Comparator #(.width(3)) comparator_26 (.a(Instruction[14:12]), .b(3'b000), .eq(comparator_26_eq));  // open: gt, lt
  and and_15 (beq, comparator_24_eq, comparator_27_eq);
  Comparator #(.width(3)) comparator_27 (.a(Instruction[14:12]), .b(3'b000), .eq(comparator_27_eq));  // open: gt, lt
  and and_16 (bge, comparator_25_eq, comparator_28_eq);
  Comparator #(.width(3)) comparator_28 (.a(Instruction[14:12]), .b(3'b101), .eq(comparator_28_eq));  // open: gt, lt
  Comparator #(.width(7)) comparator_29 (.a(7'b0010111), .b(Instruction[6:0]), .eq(auipc));  // open: gt, lt
  Comparator #(.width(7)) comparator_30 (.a(7'b1100111), .b(Instruction[6:0]), .eq(comparator_30_eq));  // open: gt, lt
  Comparator #(.width(7)) comparator_31 (.a(7'b0010011), .b(Instruction[6:0]), .eq(comparator_31_eq));  // open: gt, lt
  Comparator #(.width(7)) comparator_32 (.a(Instruction[31:25]), .b({7{1'b0}}), .eq(comparator_32_eq));  // open: gt, lt
  Comparator #(.width(3)) comparator_33 (.a(Instruction[14:12]), .b(3'b000), .eq(comparator_33_eq));  // open: gt, lt
  Comparator #(.width(7)) comparator_34 (.a(7'b0110011), .b(Instruction[6:0]), .eq(comparator_34_eq));  // open: gt, lt
  Comparator #(.width(7)) comparator_35 (
    .a(Instruction[31:25]), .b(7'b0000001), .eq(comparator_35_eq));  // open: gt, lt
  Comparator #(.width(7)) comparator_36 (.a(7'b0110011), .b(Instruction[6:0]), .eq(comparator_36_eq));  // open: gt, lt
  Comparator #(.width(7)) comparator_37 (
    .a(Instruction[31:25]), .b(7'b0000001), .eq(comparator_37_eq));  // open: gt, lt
  Comparator #(.width(7)) comparator_38 (.a(7'b0110011), .b(Instruction[6:0]), .eq(comparator_38_eq));  // open: gt, lt
  Comparator #(.width(7)) comparator_39 (.a(Instruction[31:25]), .b({7{1'b0}}), .eq(comparator_39_eq));  // open: gt, lt
  Comparator #(.width(7)) comparator_40 (.a(7'b0110011), .b(Instruction[6:0]), .eq(comparator_40_eq));  // open: gt, lt
  Comparator #(.width(7)) comparator_41 (.a(Instruction[31:25]), .b({7{1'b0}}), .eq(comparator_41_eq));  // open: gt, lt
  Comparator #(.width(7)) comparator_42 (.a(7'b0000011), .b(Instruction[6:0]), .eq(comparator_42_eq));  // open: gt, lt
  Comparator #(.width(7)) comparator_43 (.a(7'b0010011), .b(Instruction[6:0]), .eq(comparator_43_eq));  // open: gt, lt
  Comparator #(.width(3)) comparator_44 (.a(Instruction[14:12]), .b(3'b001), .eq(comparator_44_eq));  // open: gt, lt
  Comparator #(.width(3)) comparator_45 (.a(Instruction[14:12]), .b(3'b101), .eq(comparator_45_eq));  // open: gt, lt
  Comparator #(.width(7)) comparator_46 (.a(7'b0110111), .b(Instruction[6:0]), .eq(lui));  // open: gt, lt
  and and_17 (jalr, comparator_30_eq, comparator_33_eq);
  and and_18 (and_18_out, comparator_34_eq, comparator_47_eq);
  Comparator #(.width(3)) comparator_47 (.a(Instruction[14:12]), .b(3'b001), .eq(comparator_47_eq));  // open: gt, lt
  and and_19 (and_19_out, comparator_36_eq, comparator_48_eq);
  Comparator #(.width(3)) comparator_48 (.a(Instruction[14:12]), .b(3'b011), .eq(comparator_48_eq));  // open: gt, lt
  and and_20 (and_20_out, comparator_38_eq, comparator_49_eq);
  Comparator #(.width(3)) comparator_49 (.a(Instruction[14:12]), .b(3'b010), .eq(comparator_49_eq));  // open: gt, lt
  and and_21 (and_21_out, comparator_40_eq, comparator_50_eq);
  Comparator #(.width(3)) comparator_50 (.a(Instruction[14:12]), .b(3'b100), .eq(comparator_50_eq));  // open: gt, lt
  and and_22 (lhI, comparator_42_eq, comparator_51_eq);
  Comparator #(.width(3)) comparator_51 (.a(Instruction[14:12]), .b(3'b001), .eq(comparator_51_eq));  // open: gt, lt
  and and_23 (slli, comparator_43_eq, comparator_44_eq);
  and and_24 (and_24_out, comparator_31_eq, comparator_45_eq);
  and and_25 (srli, and_24_out, comparator_32_eq);
  Comparator #(.width(7)) comparator_52 (.a(7'b0100011), .b(Instruction[6:0]), .eq(comparator_52_eq));  // open: gt, lt
  Comparator #(.width(7)) comparator_53 (.a(7'b1100011), .b(Instruction[6:0]), .eq(comparator_53_eq));  // open: gt, lt
  Comparator #(.width(7)) comparator_54 (.a(7'b1100011), .b(Instruction[6:0]), .eq(comparator_54_eq));  // open: gt, lt
  and and_26 (mulhR, and_18_out, comparator_35_eq);
  and and_27 (mulhuR, and_19_out, comparator_37_eq);
  and and_28 (sltR, and_20_out, comparator_39_eq);
  and and_29 (xorR, and_21_out, comparator_41_eq);
  and and_30 (shS, comparator_52_eq, comparator_55_eq);
  Comparator #(.width(3)) comparator_55 (.a(Instruction[14:12]), .b(3'b001), .eq(comparator_55_eq));  // open: gt, lt
  and and_31 (bne, comparator_53_eq, comparator_56_eq);
  Comparator #(.width(3)) comparator_56 (.a(Instruction[14:12]), .b(3'b001), .eq(comparator_56_eq));  // open: gt, lt
  and and_32 (bltu, comparator_54_eq, comparator_57_eq);
  Comparator #(.width(3)) comparator_57 (.a(Instruction[14:12]), .b(3'b110), .eq(comparator_57_eq));  // open: gt, lt
  not not_1 (not_1_out, BrEq);
  or or_1 (or_1_out, blt, bltu);
  not not_2 (not_2_out, BrEq);
  not not_3 (not_3_out, BrLt);
  Comparator #(.width(7)) comparator_58 (.a(7'b1101111), .b(Instruction[6:0]), .eq(jal));  // open: gt, lt
  and and_33 (and_33_out, not_1_out, BrLt);
  and and_34 (and_34_out, BrEq, beq);
  and and_35 (and_35_out, not_2_out, bne);
  or or_2 (or_2_out, not_3_out, BrEq);
  or or_3 (or_3_out, bge, bgeu);
  Comparator #(.width(7)) comparator_59 (.a(7'b0010011), .b(Instruction[6:0]), .eq(comparator_59_eq));  // open: gt, lt
  Comparator #(.width(7)) comparator_60 (.a(7'b0010011), .b(Instruction[6:0]), .eq(comparator_60_eq));  // open: gt, lt
  Comparator #(.width(7)) comparator_61 (
    .a(Instruction[31:25]), .b(7'b0100000), .eq(comparator_61_eq));  // open: gt, lt
  Comparator #(.width(7)) comparator_62 (.a(Instruction[6:0]), .b(7'b1101111), .eq(comparator_62_eq));  // open: gt, lt
  Comparator #(.width(7)) comparator_63 (.a(Instruction[6:0]), .b(7'b1100111), .eq(comparator_63_eq));  // open: gt, lt
  and and_36 (and_36_out, and_33_out, or_1_out);
  or or_4 (or_4_out, and_34_out, and_35_out);
  and and_37 (and_37_out, or_2_out, or_3_out);
  Comparator #(.width(7)) comparator_64 (.a(7'b0110011), .b(Instruction[6:0]), .eq(comparator_64_eq));  // open: gt, lt
  Comparator #(.width(7)) comparator_65 (.a(Instruction[31:25]), .b({7{1'b0}}), .eq(comparator_65_eq));  // open: gt, lt
  Comparator #(.width(7)) comparator_66 (.a(7'b0110011), .b(Instruction[6:0]), .eq(comparator_66_eq));  // open: gt, lt
  Comparator #(.width(7)) comparator_67 (
    .a(Instruction[31:25]), .b(7'b0100000), .eq(comparator_67_eq));  // open: gt, lt
  Comparator #(.width(7)) comparator_68 (.a(7'b0110011), .b(Instruction[6:0]), .eq(comparator_68_eq));  // open: gt, lt
  Comparator #(.width(7)) comparator_69 (.a(Instruction[31:25]), .b({7{1'b0}}), .eq(comparator_69_eq));  // open: gt, lt
  Comparator #(.width(7)) comparator_70 (.a(7'b0110011), .b(Instruction[6:0]), .eq(comparator_70_eq));  // open: gt, lt
  Comparator #(.width(7)) comparator_71 (.a(Instruction[31:25]), .b({7{1'b0}}), .eq(comparator_71_eq));  // open: gt, lt
  Comparator #(.width(7)) comparator_72 (.a(7'b0000011), .b(Instruction[6:0]), .eq(comparator_72_eq));  // open: gt, lt
  and and_38 (slti, comparator_59_eq, comparator_73_eq);
  Comparator #(.width(3)) comparator_73 (.a(Instruction[14:12]), .b(3'b010), .eq(comparator_73_eq));  // open: gt, lt
  and and_39 (and_39_out, comparator_60_eq, comparator_74_eq);
  Comparator #(.width(3)) comparator_74 (.a(Instruction[14:12]), .b(3'b101), .eq(comparator_74_eq));  // open: gt, lt
  Comparator #(.width(7)) comparator_75 (.a(7'b0100011), .b(Instruction[6:0]), .eq(comparator_75_eq));  // open: gt, lt
  Comparator #(.width(3)) comparator_76 (.a(Instruction[14:12]), .b(3'b010), .eq(comparator_76_eq));  // open: gt, lt
  Comparator #(.width(7)) comparator_77 (.a(7'b1100011), .b(Instruction[6:0]), .eq(comparator_77_eq));  // open: gt, lt
  Comparator #(.width(3)) comparator_78 (.a(Instruction[14:12]), .b(3'b100), .eq(comparator_78_eq));  // open: gt, lt
  Comparator #(.width(7)) comparator_79 (.a(7'b1100011), .b(Instruction[6:0]), .eq(comparator_79_eq));  // open: gt, lt
  or or_5 (or_5_out, or_4_out, and_37_out);
  and and_40 (and_40_out, comparator_64_eq, comparator_80_eq);
  Comparator #(.width(3)) comparator_80 (.a(Instruction[14:12]), .b(3'b101), .eq(comparator_80_eq));  // open: gt, lt
  and and_41 (and_41_out, comparator_66_eq, comparator_81_eq);
  Comparator #(.width(3)) comparator_81 (.a(Instruction[14:12]), .b(3'b101), .eq(comparator_81_eq));  // open: gt, lt
  and and_42 (and_42_out, comparator_68_eq, comparator_82_eq);
  Comparator #(.width(3)) comparator_82 (.a(Instruction[14:12]), .b(3'b110), .eq(comparator_82_eq));  // open: gt, lt
  and and_43 (and_43_out, comparator_70_eq, comparator_83_eq);
  Comparator #(.width(3)) comparator_83 (.a(Instruction[14:12]), .b(3'b111), .eq(comparator_83_eq));  // open: gt, lt
  and and_44 (lwI, comparator_72_eq, comparator_84_eq);
  Comparator #(.width(3)) comparator_84 (.a(Instruction[14:12]), .b(3'b010), .eq(comparator_84_eq));  // open: gt, lt
  and and_45 (srai, and_39_out, comparator_61_eq);
  and and_46 (swS, comparator_75_eq, comparator_76_eq);
  and and_47 (blt, comparator_77_eq, comparator_78_eq);
  and and_48 (bgeu, comparator_79_eq, comparator_85_eq);
  Comparator #(.width(3)) comparator_85 (.a(Instruction[14:12]), .b(3'b111), .eq(comparator_85_eq));  // open: gt, lt
  buf or_6 (or_6_out, comparator_62_eq);  // OR_Gate
  or or_7 (or_7_out, comparator_63_eq, and_36_out);
  and and_49 (srlR, and_40_out, comparator_65_eq);
  and and_50 (sraR, and_41_out, comparator_67_eq);
  and and_51 (orR, and_42_out, comparator_69_eq);
  and and_52 (andR, and_43_out, comparator_71_eq);
  or or_8 (or_8_out, or_6_out, or_7_out);
  or or_9 (PCSel, or_8_out, or_5_out);
  Priority_Encoder #(.select_enc(6)) priority_encoder_1 (
    .in0(addR), .in1(mulR), .in2(subR), .in3(sllR), .in4(mulhR), .in5(mulhuR), .in6(sltR), .in7(xorR),
    .in8(srlR), .in9(sraR), .in10(orR), .in11(andR), .in12(lbI), .in13(lhI), .in14(lwI), .in15(addi),
    .in16(slli), .in17(slti), .in18(xori), .in19(srli), .in20(srai), .in21(ori), .in22(andi), .in23(sbS),
    .in24(shS), .in25(swS), .in26(beq), .in27(bne), .in28(blt), .in29(bge), .in30(bltu), .in31(bgeu),
    .in32(auipc), .in33(lui), .in34(jal), .in35(jalr), .out(InputROM));  // open: in36, in37, in38, in39, in40, in41, in42, in43, in44, in45, in46, in47, in48, in49, in50, in51, in52, in53, in54, in55, in56, in57, in58, in59, in60, in61, in62, in63, gs, en_out, en_in

  // Notes on the sheet:
  //   S TYPE 
  //   B TYPE 
  //   OPCODE
  //   OPCODE
  //   FUNC 7
  //   OPCODE
  //   FUNC 7
  //   OPCODE
  //   FUNC 7
  //   OPCODE
  //   OPCODE
  //   OPCODE
  //   OPCODE
  //   OPCODE
  //   U/J TYPE 
  //   INPUTS to your circuit
  //   OPCODE
  //   OPCODE
  //   OPCODE
  //   OPCODE
  //   contents of rom_1 (hex, n*v repeats v):
  //   1001 1401 1601 1081 1481 1581 1101 1201 1281 1681 1301 1381 41 41 41 1041 10c1 1141 1241 12c1 16c1
  //   1341 13c1 1842 1842 1842 4*1064 1074 1074 1067 17e7 2069 2041
  //   ROM FOR CONTROL LOGIC
  //   OPCODE
  //   OPCODE
  //   FUNC 7
  //   OPCODE
  //   FUNC 7
  //   OPCODE
  //   FUNC 7
  //   OPCODE
  //   OPCODE
  //   OPCODE
  //   FUNC 7
  //   DON'T CHANGE THE LOCATIONS OF THE INPUTS AND OUTPUTS!
  //   This is only if you choose to do the ROM option
  //   CONNECT
  //   WIRE
  //   TO
  //   USE
  //   ROM
  //   OPCODE
  //   OPCODE
  //   OPCODE
  //   OPCODE
  //   OPCODE
  //   OUTPUT from your circuit
  //   R TYPE 
  //   I TYPE 
  //   OPCODE
  //   OPCODE
  //   OPCODE
  //   FUNC 7
  //   OPCODE
  //   FUNC 7
  //   OPCODE
  //   FUNC 7
  //   OPCODE
  //   FUNC 7
  //   OPCODE
  //   OPCODE
  //   OPCODE
  //   OPCODE
  //   OPCODE
  //   Reminder: If using ROM, use combinational logic for PCSel
endmodule
