// Logisim project cpu.circ as structural Verilog: 1 circuit, main circuit cpu
module cpu (
  input  clk,
  input  [31:0] Instruction,
  input  [31:0] MemReadData,
  output [31:0] MemAddress,
  output [31:0] ProgramCounter,
  output [31:0] ra,
  output [31:0] sp,
  output [31:0] t0,
  output [31:0] t1,
  output [31:0] t2,
  output [31:0] s0,
  output [31:0] s1,
  output [31:0] a0,
  output [3:0] MemWriteMask,
  output [31:0] MemWriteData
);

  wire ASel, branch_comp_1_breq, branch_comp_1_brlt, Brun, BSel, MemWEn, PCSel, RegWEn;
  wire [1:0] WBSel;
  wire [2:0] ImmSel;
  wire [3:0] ALUSel;
  wire [31:0] ASel_output, BSel_output, datatoReg, IMM, Instruction1, multiplexer_1_out, multiplexer_4_out,
       PCplus4, PCplus4new, ProgramCounter1, ReadData1, ReadData2, Writedata;

  Multiplexer #(.width(32)) multiplexer_1 (.in0(PCplus4), .in1(MemAddress), .out(multiplexer_1_out), .sel(PCSel));
  control_logic control_logic_1 (
    .PCSel(PCSel), .RegWEn(RegWEn), .ImmSel(ImmSel), .BrUn(Brun), .ASel(ASel), .BSel(BSel), .ALUSel(ALUSel),
    .MemWEn(MemWEn), .WBSel(WBSel), .Instruction(Instruction1), .BrEq(branch_comp_1_breq),
    .BrLt(branch_comp_1_brlt));
  Register #(.width(32)) PC (.D(multiplexer_1_out), .clk(clk), .Q(ProgramCounter));  // open: en, clr
  branch_comp branch_comp_1 (
    .BrData1(ReadData1), .BrData2(ReadData2), .BrUn(Brun), .BrEq(branch_comp_1_breq),
    .BrLt(branch_comp_1_brlt));
  Adder #(.width(32)) adder_1 (.a(32'h4), .b(ProgramCounter), .out(PCplus4));  // open: cin, cout
  regfile regfile_1 (
    .ReadIndex1(Instruction1[19:15]), .ReadIndex2(Instruction1[24:20]), .WriteIndex(Instruction1[11:7]),
    .WriteData(Writedata), .RegWEn(RegWEn), .clk(clk), .ra(ra), .sp(sp), .t0(t0), .t1(t1), .t2(t2), .s0(s0),
    .s1(s1), .a0(a0), .ReadData1(ReadData1), .ReadData2(ReadData2));
  imm_gen imm_gen_1 (.Instruction(Instruction1), .ImmSel(ImmSel), .Immediate(IMM));
  Register #(.width(32)) Pipe_PC (.D(ProgramCounter), .clk(clk), .Q(ProgramCounter1));  // open: en, clr
  Multiplexer #(.width(32)) multiplexer_2 (.in0(ReadData1), .in1(ProgramCounter1), .out(ASel_output), .sel(ASel));
  Multiplexer #(.width(32)) multiplexer_3 (.in0(ReadData2), .in1(IMM), .out(BSel_output), .sel(BSel));
  partial_load partial_load_1 (
    .Instruction(Instruction1), .MemAddress(MemAddress), .DataFromMem(MemReadData), .DataToReg(datatoReg));
  alu alu_1 (.ALUResult(MemAddress), .A(ASel_output), .B(BSel_output), .ALUSel(ALUSel));
  Multiplexer #(.width(32)) multiplexer_4 (.in0(Instruction), .in1(32'h1300013), .out(multiplexer_4_out), .sel(PCSel));
  Register #(.width(32)) Pipe_INST (.D(multiplexer_4_out), .clk(clk), .Q(Instruction1));  // open: en, clr
  Adder #(.width(32)) adder_2 (.a(32'h4), .b(ProgramCounter1), .out(PCplus4new));  // open: cin, cout
  partial_store partial_store_1 (
    .Instruction(Instruction1), .MemAddress(MemAddress), .DataFromReg(ReadData2), .MemWEn(MemWEn),
    .MemWriteMask(MemWriteMask), .DataToMem(MemWriteData));
  Multiplexer #(.select(2), .width(32)) multiplexer_5 (
    .in0(datatoReg), .in1(MemAddress), .in2(PCplus4new), .out(Writedata), .sel(WBSel));  // open: in3

  // Other names for the same wires on the sheet: ALU_output[31:0] = MemAddress

  // Notes on the sheet:
  //   To IMEM
  //   IMEM (do **NOT** move this)
  //   From IMEM
  //   Inputs/Outputs for testing. Do **NOT** move these.
  //   It is OK to move the PC, RegFile, ALU, MEM, Branch Comp, Imm Gen, Partial Load, Partial Store and Control Logic to wherever is most convenient for you when constructing your CPU, and to delete this text
  //   To DMEM
  //   DMEM (do **NOT** move this)
  //   From DMEM
endmodule
