// Logisim project partial-load.circ as structural Verilog: 1 circuit, main circuit partial_load
module partial_load (
  input  [31:0] Instruction,
  input  [31:0] MemAddress,
  input  [31:0] DataFromMem,
  output [31:0] DataToReg
);

  wire and_1_out, and_2_out, and_3_out, and_4_out, and_5_out, and_6_out, and_7_out, lb, lh, lw, one, three,
       two, zero;
  wire [1:0] whichLB, whichLH, whichmem;
  wire [31:0] bit_extender_1_out, bit_extender_2_out, bit_extender_3_out, bit_extender_4_out,
       bit_extender_5_out, bit_extender_6_out, bit_extender_7_out, lb_output, lh_output;

  Comparator #(.width(3)) comparator_1 (.a(3'b000), .b(Instruction[14:12]), .eq(lb));  // open: gt, lt
  Comparator #(.width(3)) comparator_2 (.a(3'b001), .b(Instruction[14:12]), .eq(lh));  // open: gt, lt
  Comparator #(.width(3)) comparator_3 (.a(3'b010), .b(Instruction[14:12]), .eq(lw));  // open: gt, lt
  Comparator #(.width(2)) comparator_4 (.a(2'b00), .b(MemAddress[1:0]), .eq(zero));  // open: gt, lt
  Comparator #(.width(2)) comparator_5 (.a(2'b01), .b(MemAddress[1:0]), .eq(one));  // open: gt, lt
  Comparator #(.width(2)) comparator_6 (.a(2'b10), .b(MemAddress[1:0]), .eq(two));  // open: gt, lt
  Comparator #(.width(2)) comparator_7 (.a(2'b11), .b(MemAddress[1:0]), .eq(three));  // open: gt, lt
  and and_1 (and_1_out, zero, lb);
  and and_2 (and_2_out, one, lb);
  and and_3 (and_3_out, two, lb);
  and and_4 (and_4_out, three, lb);
  Priority_Encoder #(.select_enc(2)) priority_encoder_1 (
    .in0(lb), .in1(lh), .in2(lw), .out(whichmem));  // open: in3, gs, en_out, en_in
  Priority_Encoder #(.select_enc(2)) priority_encoder_2 (
    .in0(and_1_out), .in1(and_2_out), .in2(and_3_out), .in3(and_4_out), .out(whichLB));  // open: gs, en_out, en_in
  assign bit_extender_1_out = {{24{DataFromMem[7]}}, DataFromMem[7:0]};  // Bit_Extender bit_extender_1
  assign bit_extender_2_out = {{24{DataFromMem[15]}}, DataFromMem[15:8]};  // Bit_Extender bit_extender_2
  assign bit_extender_3_out = {{24{DataFromMem[23]}}, DataFromMem[23:16]};  // Bit_Extender bit_extender_3
  assign bit_extender_4_out = {{24{DataFromMem[31]}}, DataFromMem[31:24]};  // Bit_Extender bit_extender_4
  Multiplexer #(.select(2), .width(32)) multiplexer_1 (
    .in0(bit_extender_1_out), .in1(bit_extender_2_out), .in2(bit_extender_3_out), .in3(bit_extender_4_out),
    .out(lb_output), .sel(whichLB));
  Multiplexer #(.select(2), .width(32)) multiplexer_2 (
    .in0(lb_output), .in1(lh_output), .in2(DataFromMem), .out(DataToReg), .sel(whichmem));  // open: in3
  and and_5 (and_5_out, zero, lh);
  and and_6 (and_6_out, one, lh);
  and and_7 (and_7_out, two, lh);
  assign bit_extender_5_out = {{16{DataFromMem[15]}}, DataFromMem[15:0]};  // Bit_Extender bit_extender_5
  assign bit_extender_6_out = {{16{DataFromMem[23]}}, DataFromMem[23:8]};  // Bit_Extender bit_extender_6
  assign bit_extender_7_out = {{16{DataFromMem[31]}}, DataFromMem[31:16]};  // Bit_Extender bit_extender_7
  Priority_Encoder #(.select_enc(2)) priority_encoder_3 (
    .in0(and_5_out), .in1(and_6_out), .in2(and_7_out), .out(whichLH));  // open: in3, gs, en_out, en_in
  Multiplexer #(.select(2), .width(32)) multiplexer_3 (
    .in0(bit_extender_5_out), .in1(bit_extender_6_out), .in2(bit_extender_7_out), .out(lh_output),
    .sel(whichLH));  // open: in3

  // Notes on the sheet:
  //   INPUTS to your circuit
  //   DON'T CHANGE THE LOCATIONS OF THE INPUTS AND OUTPUTS!
  //   OUTPUT from your circuit
endmodule
