// Logisim project partial-store.circ as structural Verilog: 1 circuit, main circuit partial_store
module partial_store (
  input  [31:0] Instruction,
  input  [31:0] MemAddress,
  input  [31:0] DataFromReg,
  input  MemWEn,
  output [3:0] MemWriteMask,
  output [31:0] DataToMem
);

  wire and_1_out, and_2_out, and_3_out, and_4_out, and_5_out, and_6_out, and_7_out, and_8_out, and_9_out,
       and_10_out, and_11_out, and_12_out, not_1_out, one, sb, sh, sw, three, two, zero;
  wire [1:0] whichmem, whichSB, whichSH;
  wire [3:0] mask;
  wire [31:0] sb_output, sh_output;

  Comparator #(.width(2)) comparator_1 (.a(2'b00), .b(MemAddress[1:0]), .eq(zero));  // open: gt, lt
  Comparator #(.width(2)) comparator_2 (.a(2'b01), .b(MemAddress[1:0]), .eq(one));  // open: gt, lt
  Comparator #(.width(2)) comparator_3 (.a(2'b10), .b(MemAddress[1:0]), .eq(two));  // open: gt, lt
  Comparator #(.width(2)) comparator_4 (.a(2'b11), .b(MemAddress[1:0]), .eq(three));  // open: gt, lt
  Comparator #(.width(3)) comparator_5 (.a(3'b000), .b(Instruction[14:12]), .eq(sb));  // open: gt, lt
  Comparator #(.width(3)) comparator_6 (.a(3'b001), .b(Instruction[14:12]), .eq(sh));  // open: gt, lt
  Comparator #(.width(3)) comparator_7 (.a(3'b010), .b(Instruction[14:12]), .eq(sw));  // open: gt, lt
  and and_1 (and_1_out, zero, sb);
  and and_2 (and_2_out, one, sb);
  and and_3 (and_3_out, two, sb);
  and and_4 (and_4_out, three, sb);
  Priority_Encoder #(.select_enc(2)) priority_encoder_1 (
    .in0(sb), .in1(sh), .in2(sw), .out(whichmem));  // open: in3, gs, en_out, en_in
  Priority_Encoder #(.select_enc(2)) priority_encoder_2 (
    .in0(and_1_out), .in1(and_2_out), .in2(and_3_out), .in3(and_4_out), .out(whichSB));  // open: gs, en_out, en_in
  Multiplexer #(.select(2), .width(32)) multiplexer_1 (
    .in0({{24{1'b0}}, DataFromReg[7:0]}), .in1({{16{1'b0}}, DataFromReg[7:0], {8{1'b0}}}),
    .in2({{8{1'b0}}, DataFromReg[7:0], {16{1'b0}}}), .in3({DataFromReg[7:0], {24{1'b0}}}), .out(sb_output),
    .sel(whichSB));
  and and_5 (and_5_out, zero, sh);
  and and_6 (and_6_out, two, sh);
  Multiplexer #(.select(2), .width(32)) multiplexer_2 (
    .in0(sb_output), .in1(sh_output), .in2(DataFromReg), .out(DataToMem), .sel(whichmem));  // open: in3
  Priority_Encoder #(.select_enc(2)) priority_encoder_3 (
    .in0(and_5_out), .in1(and_6_out), .out(whichSH));  // open: in2, in3, gs, en_out, en_in
  Multiplexer #(.select(2), .width(32)) multiplexer_3 (
    .in0({{16{1'b0}}, DataFromReg[15:0]}), .in1({DataFromReg[15:0], {16{1'b0}}}), .out(sh_output),
    .sel(whichSH));  // open: in2, in3
  and and_7 (and_7_out, zero, sb);
  and and_8 (and_8_out, one, sb);
  and and_9 (and_9_out, two, sb);
  and and_10 (and_10_out, three, sb);
  and and_11 (and_11_out, zero, sh);
  and and_12 (and_12_out, two, sh);
  not not_1 (not_1_out, MemWEn);
  Priority_Encoder #(.select_enc(4)) priority_encoder_4 (
    .in0(and_7_out), .in1(and_8_out), .in2(and_9_out), .in3(and_10_out), .in4(and_11_out), .in5(and_12_out),
    .in6(sw), .in15(not_1_out), .out(mask));  // open: in7, in8, in9, in10, in11, in12, in13, in14, gs, en_out, en_in
  Multiplexer #(.select(4), .width(4)) multiplexer_4 (
    .in0(4'b0001), .in1(4'b0010), .in2(4'b0100), .in3(4'b1000), .in4(4'b0011), .in5(4'b1100), .in6(4'b1111),
    .in15(4'b0000), .out(MemWriteMask), .sel(mask));  // open: in7, in8, in9, in10, in11, in12, in13, in14

  // Notes on the sheet:
  //   INPUTS to your circuit
  //   DON'T CHANGE THE LOCATIONS OF THE INPUTS AND OUTPUTS!
  //   OUTPUT from your circuit
endmodule
